# Fritzing sketch MOTUS (saved by Fritzing 0.9.3b)
breadboards: 1

parts:
  Raspberry_Pi_1 = Raspberry Pi 3 [part_number=RPI-3-V1.2]
  Accelerometer = Triple Axis Accelerometer Breakout - ADXL345
  LED_Indicator = smd LED [color="Red (633nm)" package="0603 [SMD]"]
  Motion_Sensor = HC-SR501 Body Sensor Module
  U1 = TCM8240MD [package=tcm8240md]  # not connected
  R1 = Resistor [tolerance=±5% resistance=300 package="1206 [SMD]"]

nets:
  3V3: Raspberry_Pi_1.3v3, Accelerometer.VCC
  N1: Raspberry_Pi_1.GPIO2, Accelerometer.SDA
  N2: Raspberry_Pi_1.GPIO3, Accelerometer.SCL
  N3: Raspberry_Pi_1.GIPO4, Motion_Sensor.OUT
  N4: Raspberry_Pi_1.GIPO17, LED_Indicator.anode
  GND: Raspberry_Pi_1.GND, Accelerometer.GND, Motion_Sensor.GND, R1.Pin_0
  5V: Raspberry_Pi_1.5V, Motion_Sensor.VCC
  N5: LED_Indicator.cathode, R1.Pin_1

notes:
  Pi Camera Connected to Pi Camera Interface
  Wire Types:
  Red - 5V
  Orange - 3.3V
  Black - GND
  Blue - SDA
  Cyan - SCL
  Brown - GPIO4
  Purple - GPIO17

custom parts:
  HC-SR501 Body Sensor Module: Pyroelectric Infrared PIR Motion Sensor Detector Module
